# Fritzing sketch miniMO_breadboard (saved by Fritzing 0.9.3b)
breadboards: 1

parts:
  S1 = Pushbutton [package="[SMD]"]
  U1 = attiny85 [package=dip]  # not connected
  C1 = Ceramic Capacitor [capacitance=100nF package="100 mil [THT, multilayer]"]
  R1 = Resistor [tolerance=±5% resistance=10k package=THT]
  C2 = Ceramic Capacitor [capacitance=100nF package="100 mil [THT, multilayer]"]
  C3 = Ceramic Capacitor [capacitance=100nF package="100 mil [THT, multilayer]"]
  R2 = Trimmer Potentiometer [maximum_resistance=10kΩ package=THT]
  LED1 = smd LED [color="Red (633nm)" package="0603 [SMD]"]
  R3 = Resistor [tolerance=±5% resistance=470 package="2512 [SMD]"]
  R4 = Resistor [tolerance=±5% resistance=100 package="1206 [SMD]"]
  R5 = Resistor [tolerance=±5% resistance=10k package="1206 [SMD]"]
  R6 = Resistor [tolerance=±5% resistance=1M package="1206 [SMD]"]
  J1 = double row male pin header, 2 pins [form="♂ (male)"]
  J2 = double row male pin header, 2 pins [form="♂ (male)"]
  J3 = double row male pin header, 2 pins [form="♂ (male)"]
  J4 = double row male pin header, 2 pins [form="♂ (male)"]
  J5 = female pin header, 5 pins [form="♀ (female)"]
  R7 = Resistor [tolerance=±5% resistance=10k package="1206 [SMD]"]

nets:
  N1: S1.Pin_1, S1.Pin_2, C2.0, R2.leg2, R6.Pin_1
  N2: S1.Pin_3, S1.Pin_4, J5.pin4, R7.Pin_1
  N3: C1.0, C2.1, C3.1, R2.leg1, R4.Pin_1, J1.pin1, J2.pin1, J3.pin1, J4.pin2, J5.pin1, R7.Pin_0
  N4: C1.1, R1.Pin_1, R5.Pin_0
  N5: R1.Pin_0, R2.wiper
  N6: C3.0, R3.Pin_1, J3.pin2, J4.pin1
  N7: LED1.cathode, J5.pin3
  N8: LED1.anode, R4.Pin_0
  N9: R5.Pin_1, J1.pin2
  N10: R6.Pin_0, J2.pin2, J5.pin5

notes:
  inverted U
  10K
  1M
  100Ω
  470Ω
